// Digital circuit CPU.dig as structural Verilog
module CPU (
  input  clk,
  input  CLR_PC,
  input  [7:0] IN,
  input  STR
);

  wire alu_1_p5, comparator_1_eq, comparator_2_eq, comparator_3_eq, comparator_4_eq, comparator_5_eq,
       comparator_6_eq, comparator_7_eq, comparator_8_eq, comparator_9_eq, comparator_10_eq,
       dat_to_adr_interface_1_p7;
  wire [3:0] register_2_val;
  wire [7:0] flash_memory_1_q_cmd, programme_counter_1_p1;
  wire [7:4] register_2_val_2;
  wire [15:0] programme_counter_1_p2, programme_counter_1_p7;

  Comparator #(.Bits(8)) comparator_1 (.a(flash_memory_1_q_cmd), .b(8'h1), .eq(comparator_1_eq));  // open: gt, lt
  Comparator #(.Bits(8)) comparator_2 (.a(flash_memory_1_q_cmd), .b(8'h2), .eq(comparator_2_eq));  // open: gt, lt
  Comparator #(.Bits(8)) comparator_3 (.a(flash_memory_1_q_cmd), .b(8'h3), .eq(comparator_3_eq));  // open: gt, lt
  Comparator #(.Bits(8)) comparator_4 (.a(flash_memory_1_q_cmd), .b(8'h4), .eq(comparator_4_eq));  // open: gt, lt
  Comparator #(.Bits(8)) comparator_5 (.a(flash_memory_1_q_cmd), .b(8'h5), .eq(comparator_5_eq));  // open: gt, lt
  Comparator #(.Bits(8)) comparator_6 (.a(flash_memory_1_q_cmd), .b(8'h6), .eq(comparator_6_eq));  // open: gt, lt
  Comparator #(.Bits(8)) comparator_7 (.a(flash_memory_1_q_cmd), .b(8'h7), .eq(comparator_7_eq));  // open: gt, lt
  Comparator #(.Bits(8)) comparator_8 (.a(flash_memory_1_q_cmd), .b(8'h24), .eq(comparator_8_eq));  // open: gt, lt
  Comparator #(.Bits(8)) comparator_9 (.a(flash_memory_1_q_cmd), .b(8'h25), .eq(comparator_9_eq));  // open: gt, lt
  Comparator #(.Bits(8)) comparator_10 (.a(flash_memory_1_q_cmd), .b(8'h26), .eq(comparator_10_eq));  // open: gt, lt
  // Programme_Counter programme_counter_1: pin names not known; wires that end beside it: programme_counter_1_p1, programme_counter_1_p2, clk, comparator_1_eq, comparator_2_eq, CLR_PC, programme_counter_1_p7
  Flash_Memory flash_memory_1 (
    .LN(programme_counter_1_p7), .DAT_dis(alu_1_p5), .ADR_dis(dat_to_adr_interface_1_p7), .CLK(clk),
    .Q_CMD(flash_memory_1_q_cmd), .Q_DAT(programme_counter_1_p1), .Q_ADR(programme_counter_1_p2));
  // ALU alu_1: pin names not known; wires that end beside it: flash_memory_1_q_cmd, programme_counter_1_p1, clk, programme_counter_1_p1, alu_1_p5
  // DAT_to_ADR_interface dat_to_adr_interface_1: pin names not known; wires that end beside it: programme_counter_1_p1, comparator_3_eq, comparator_4_eq, comparator_5_eq, clk, programme_counter_1_p2, dat_to_adr_interface_1_p7
  RAM ram_1 (
    .DAT(programme_counter_1_p1), .ADR(programme_counter_1_p2), .STR(comparator_6_eq), .LD(comparator_7_eq),
    .CLK(clk), .Q_DAT(programme_counter_1_p1));
  Register register_1 (.D(IN), .STR(comparator_8_eq), .LD(STR), .CLK(clk), .Q(programme_counter_1_p1));  // open: VAL
  Register register_2 (
    .D(programme_counter_1_p1), .STR(comparator_9_eq), .LD(comparator_10_eq), .CLK(clk),
    .VAL({register_2_val_2, register_2_val}), .Q(programme_counter_1_p1));
  Seven_Seg_Hex seven_seg_hex_1 (.d(register_2_val), .dp(1'b0));
  Seven_Seg_Hex seven_seg_hex_2 (.d(register_2_val_2), .dp(1'b0));

  // Notes on the sheet:
  //   clk: Hz: 5
  //   CMD
  //   LN: output from the programmme counter,
  //   the current line of code being executed
  //   DAT
  //   ADR
  //   CLK
  //   commands requiring the address bus to be disabled:
  //   Bus Transfer:
  //   - load from interface registers
  //   commands requiring the data bus to be disabled:
  //   Storage: 
  //   - load > data
  //   ALU:
  //   - add > data
  //   - add with carry > data
  //   - subtract > data
  //   incrementor:
  //   - increment > data
  //   - decrement > data
  //   logic:
  //   - binary not
  //   - binary or
  //   - binary and
  //   - binary xor
  //   - bitwise not
  //   - bitwise or
  //   - bitwise and
  //   - bitwise xor
  //   a/b/c registers:
  //   - load a > data
  //   - load b > data
  //   - load c > data
  //   compare:
  //   - bigger > data
  //   - equal > data
  //   - smaller > data
  //   flag reg:
  //   - load carry > data
  //   - load overflow > data
  //   - load flags > data
endmodule
